# Fritzing sketch Einzelwertanzeige (saved by Fritzing 0.9.3b)
circuit board: 4.86276cm x 6.67141cm
breadboards: 1

parts:
  U1 = 7-SEGMENT-DISPLAY [package=7-segment-display]
  J1 = male pin header, 8 pins [form="♂ (male)"]
  J2 = male pin header, 8 pins [form="♂ (male)"]
  U2 = 7-SEGMENT-DISPLAY [package=7-segment-display]

nets:
  N1: U1.G1, J2.pin8
  N2: J1.pin2, U2.G1
  N3: J1.pin3, U2.A
  N4: J1.pin4, U2.B
  N5: J1.pin6, U2.D
  N6: J2.pin1, U2.G
  N7: J2.pin2, U2.F
  N8: J2.pin4, U2.DP
  N9: J2.pin6, U2.E
  N10: J2.pin7, U2.C
